# Fritzing sketch mood_cube (saved by Fritzing 1.0.7)
breadboards: 2

parts:
  cubeGrip = Microbit (basic)
  4_5VDC_1 = Battery [internal_resistance=0.1Ω]
  NJU7043D = IC, DIP package, 8 pins [chip_label=7043D]
  C1 = Ceramic Capacitor [capacitance=0.1µF voltage=50V package="100 mil [THT, multilayer]"]
  R1 = Resistor [tolerance=±5% power=0.25W resistance=4.7k package=THT]
  2SC1815_1 = NPN-Transistor [package="TO92 [THT]"]
  D1 = Rectifier Diode [part_number=1N4007 package="300 mil [THT]"]
  R2 = Resistor [tolerance=±5% power=0.25W resistance=220 package=THT]
  Vibrator1 = DC Motor [voltage_(max)=6V voltage_(min)=3V]
  cubeTouch = Microbit (basic)
  4_5VDC_2 = Battery [internal_resistance=0.1Ω]
  2SC1815_2 = NPN-Transistor [package="TO92 [THT]"]
  D2 = Rectifier Diode [part_number=1N4007 package="300 mil [THT]"]
  R4 = Resistor [tolerance=±5% power=0.25W resistance=220 package=THT]
  R3 = Textile Analog Pressure Sensor [part_number=LCX-300]
  Aluminum-Mesh = Antenna
  Vibrator2 = DC Motor [voltage_(max)=6V voltage_(min)=3V]
  PL9823_1 = RGB LED PL9823 F5 [package="5 mm [THT]"]
  PL9823_2 = RGB LED PL9823 F5 [package="5 mm [THT]"]

nets:
  N1: cubeGrip.P0, NJU7043D.pin1, NJU7043D.pin2
  N2: cubeGrip.P1, R2.Pin_1
  N3: cubeGrip.P2, PL9823_1.DIN
  N4: cubeGrip.3V3, NJU7043D.pin8, C1.0, R1.Pin_0
  N5: cubeGrip.Bat_-, 4_5VDC_1.-, NJU7043D.pin4, NJU7043D.pin5, C1.1, 2SC1815_1.E, R3.pin_1, PL9823_1.GND
  N6: cubeGrip.Bat_+, 4_5VDC_1.+, D1.cathode, Vibrator1.pin_1, PL9823_1.VDD
  N7: NJU7043D.pin3, R1.Pin_1, R3.pin_0
  N8: NJU7043D.pin6, NJU7043D.pin7
  N9: 2SC1815_1.B, R2.Pin_0
  N10: 2SC1815_1.C, D1.anode, Vibrator1.pin_2
  N11: cubeTouch.P0, Aluminum-Mesh.antenna_lead
  N12: cubeTouch.P1, R4.Pin_1
  N13: cubeTouch.P2, PL9823_2.DIN
  N14: cubeTouch.Bat_-, 4_5VDC_2.-, 2SC1815_2.E, PL9823_2.GND
  N15: cubeTouch.Bat_+, 4_5VDC_2.+, D2.cathode, Vibrator2.pin_1, PL9823_2.VDD
  N16: 2SC1815_2.B, R4.Pin_0
  N17: 2SC1815_2.C, D2.anode, Vibrator2.pin_2

notes:
  cubeGrip
  cubeTouch
  4.5VDC (AAx3)

custom parts:
  Microbit (basic): BBC Microbit Fritzing part. May 2019 expanded to include schematic and pcb views as well as breadboard. PCB view assumes an Adafruit PRODUCT ID: 3342 2x40 Right Angle through hole edge connector (although others will probably work as well). The pcb svg is custom (see forum article http://forum.fritzing.org/t/making-edge-connectors-and-both-side-smd-parts/7287 for an explaination if you need to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
  RGB LED PL9823 F5: A 5mm tri-color LED with red, green and blue inside. this led includes WS2811 controller.
